// Logisim project mux.circ as structural Verilog: 6 circuits, main circuit main
module main (
  input  [1:0] in_1,
  input  [1:0] in_2,
  input  [1:0] in_3,
  input  [1:0] in_4,
  input  [1:0] in_5,
  output [1:0] out_6
);

  mux4 mux4_1 (
    .in_3(in_2[0]), .in_4(in_3[0]), .in_5(in_4[0]), .in_6(in_5[0]), .in_1(in_1[0]), .in_2(in_1[1]),
    .out_7(out_6[0]));
  mux4 mux4_2 (
    .in_3(in_2[1]), .in_4(in_3[1]), .in_5(in_4[1]), .in_6(in_5[1]), .in_1(in_1[0]), .in_2(in_1[1]),
    .out_7(out_6[1]));
endmodule

module \and  (
  input  in_1,
  input  in_2,
  output out_3
);

  wire transistor_2_out;

  Transistor transistor_1 (.in(1'b0), .out(out_3), .gate(in_2));
  Transistor #(.\type ("n")) transistor_2 (.in(1'b1), .out(transistor_2_out), .gate(in_1));
  Transistor #(.\type ("n")) transistor_3 (.in(transistor_2_out), .out(out_3), .gate(in_2));
  Transistor transistor_4 (.in(1'b0), .out(out_3), .gate(in_1));
endmodule

module \or  (
  input  in_1,
  input  in_2,
  output out_3
);

  wire transistor_4_out;

  Transistor #(.\type ("n")) transistor_1 (.in(1'b1), .out(out_3), .gate(in_1));
  Transistor #(.\type ("n")) transistor_2 (.in(1'b1), .out(out_3), .gate(in_2));
  Transistor transistor_3 (.in(transistor_4_out), .out(out_3), .gate(in_2));
  Transistor transistor_4 (.in(1'b0), .out(transistor_4_out), .gate(in_1));
endmodule

module \not  (
  input  in_1,
  output out_2
);

  Transistor transistor_1 (.in(1'b1), .out(out_2), .gate(in_1));
  Transistor #(.\type ("n")) transistor_2 (.in(1'b0), .out(out_2), .gate(in_1));
endmodule

module multiplexer (
  input  in_1,
  input  in_2,
  input  in_3,
  output out_4
);

  wire and_gate_2_out_3, and_gate_out_3, Not_out_2;

  \not  Not (.in_1(in_2), .out_2(Not_out_2));
  \and  and_gate (.in_1(in_1), .in_2(Not_out_2), .out_3(and_gate_out_3));
  \and  and_gate_2 (.in_1(in_2), .in_2(in_3), .out_3(and_gate_2_out_3));
  \or  or_1 (.in_1(and_gate_out_3), .in_2(and_gate_2_out_3), .out_3(out_4));
endmodule

module mux4 (
  input  in_1,
  input  in_2,
  input  in_3,
  input  in_4,
  input  in_5,
  input  in_6,
  output out_7
);

  wire multiplexer_1_out_4, multiplexer_2_out_4;

  multiplexer multiplexer_1 (.in_1(in_3), .in_2(in_1), .in_3(in_4), .out_4(multiplexer_1_out_4));
  multiplexer multiplexer_2 (.in_1(in_5), .in_2(in_1), .in_3(in_6), .out_4(multiplexer_2_out_4));
  multiplexer multiplexer_3 (.in_1(multiplexer_1_out_4), .in_2(in_2), .in_3(multiplexer_2_out_4), .out_4(out_7));
endmodule
