// Logisim project my_name.circ as structural Verilog: 1 circuit, main circuit main
module main (
);

  DotMatrix #(.inputtype("row"), .matrixcols(16), .matrixrows(16)) dotmatrix_1 (
    .row0({16{1'b0}}), .row1(16'hfdfe), .row2(16'hfd80), .row3(16'hdfe), .row4(16'h7dfe), .row5(16'h67ff),
    .row6(16'h7fff), .row7(16'hf76), .row8(16'hf7e), .row9(16'hf3c), .row10(16'h1f7c), .row11(16'h7bef),
    .row12(16'h7bef), .row13(16'hbef), .row14(16'h7bc7), .row15(16'h200));
  DotMatrix #(.inputtype("row"), .matrixcols(16), .matrixrows(16)) dotmatrix_2 (
    .row0({16{1'b0}}), .row1(16'h1830), .row2(16'h1bff), .row3(16'h1bff), .row4(16'hfffe), .row5(16'hfffe),
    .row6(16'h3b36), .row7(16'h3ffe), .row8(16'h7ffe), .row9(16'hf8f8), .row10(16'hd9fc), .row11(16'h1bbf),
    .row12(16'h1fb7), .row13(16'h1e33), .row14(16'h1e33), .row15(16'h1e20));
  DotMatrix #(.inputtype("row"), .matrixcols(16), .matrixrows(16)) dotmatrix_3 (
    .row0(16'h6318), .row1(16'h7318), .row2(16'h7ff8), .row3(16'h3fff), .row4(16'hfff), .row5(16'heff6),
    .row6(16'hfff6), .row7(16'h3ffe), .row8(16'hcfc), .row9(16'h3fdc), .row10(16'h3cdc), .row11(16'h7fdc),
    .row12(16'h6ffe), .row13(16'h6cf7), .row14(16'heff7), .row15(16'h20));
endmodule
