// Logisim project exp3.circ as structural Verilog
module SR_latch (
  input  RESET,
  input  SET,
  output Q,
  output nQ
);

  NOR_from_NAND nor_from_nand_1 (.in_1(RESET), .in_2(nQ), .out_3(Q));
  NOR_from_NAND nor_from_nand_2 (.in_1(Q), .in_2(SET), .out_3(nQ));
endmodule

module NOR_from_NAND (
  input  in_1,
  input  in_2,
  output out_3
);

  wire nand_1_out, nand_2_out, nand_3_out;

  nand nand_1 (nand_1_out, in_1, in_1);
  nand nand_2 (nand_2_out, in_2, in_2);
  nand nand_3 (nand_3_out, nand_1_out, nand_2_out);
  nand nand_4 (out_3, nand_3_out, nand_3_out);
endmodule

module D_Flip_Flop_SYNC (
  input  clock,
  input  in_2,
  input  set,
  output out_4,
  output out_5
);

  wire or_1_out;

  or or_1 (or_1_out, in_2, set);
  D_flip_flop d_flip_flop_1 (.in_1(clock), .in_2(or_1_out), .out_3(out_4), .out_4(out_5));
endmodule

module D_flip_flop (
  input  in_1,
  input  in_2,
  output out_3,
  output out_4
);

  wire d_latch_1_out_3, not_1_out;

  not not_1 (not_1_out, in_1);
  D_latch d_latch_1 (.CLK(not_1_out), .D(in_2), .out_3(d_latch_1_out_3));  // open: out_4
  D_latch d_latch_2 (.CLK(in_1), .D(d_latch_1_out_3), .out_3(out_3), .out_4(out_4));
endmodule

module D_latch (
  input  CLK,
  input  D,
  output out_3,
  output out_4
);

  wire and_1_out, and_2_out, not_1_out;

  not not_1 (not_1_out, D);
  and and_1 (and_1_out, CLK, not_1_out);
  and and_2 (and_2_out, CLK, D);
  SR_latch sr_latch_1 (.RESET(and_1_out), .SET(and_2_out), .Q(out_3), .nQ(out_4));
endmodule

module D_flip_flop_async (
  input  in_1,
  input  in_2,
  input  in_3,
  input  in_4,
  output out_5,
  output out_6
);

  wire nand_1_out, nand_2_out, nand_3_out, nand_4_out;

  nand nand_1 (nand_1_out, in_1, nand_4_out, nand_2_out);
  nand nand_2 (nand_2_out, nand_1_out, in_2, in_4);
  nand nand_3 (nand_3_out, nand_2_out, in_2, nand_4_out);
  nand nand_4 (nand_4_out, nand_3_out, in_3, in_4);
  nand nand_5 (out_5, in_1, nand_2_out, out_6);
  nand nand_6 (out_6, out_5, nand_3_out, in_4);
endmodule

module _0_15_counter (
  input  in_1,
  input  in_2,
  output [3:0] out_3
);

  wire [3:0] adder_1_out;

  Adder #(.width(4)) adder_1 (.a(out_3), .b(4'b0000), .out(adder_1_out), .cin(1'b1));  // open: cout
  // Probe on adder_1_out
  _4_bit_register u_4_bit_register_1 (.in_1(adder_1_out), .out_4(out_3), .in_2(in_1), .in_3(in_2));
endmodule

module _4_bit_register (
  input  [3:0] in_1,
  input  in_2,
  input  in_3,
  output [3:0] out_4
);

  D_flip_flop_async d_flip_flop_async_1 (
    .in_1(1'b1), .out_5(out_4[0]), .in_2(in_2), .in_3(in_1[0]), .in_4(in_3));  // open: out_6
  D_flip_flop_async d_flip_flop_async_2 (
    .in_1(1'b1), .out_5(out_4[1]), .in_2(in_2), .in_3(in_1[1]), .in_4(in_3));  // open: out_6
  D_flip_flop_async d_flip_flop_async_3 (
    .in_1(1'b1), .out_5(out_4[2]), .in_2(in_2), .in_3(in_1[2]), .in_4(in_3));  // open: out_6
  D_flip_flop_async d_flip_flop_async_4 (
    .in_1(1'b1), .out_5(out_4[3]), .in_2(in_2), .in_3(in_1[3]), .in_4(in_3));  // open: out_6
endmodule

module async_dff_test (
  input  in_1,
  input  in_2,
  input  in_3,
  output out_4,
  output out_5
);

  wire and_1_out, and_2_out, d_latch_1_out_3, not_1_out, or_1_out, or_2_out;

  or or_1 (or_1_out, ~in_3, not_1_out);  // OR_Gate
  not not_1 (not_1_out, in_1);
  and and_1 (and_1_out, in_2, in_3);
  D_latch d_latch_1 (.CLK(or_1_out), .D(and_1_out), .out_3(d_latch_1_out_3));  // open: out_4
  or or_2 (or_2_out, in_1, ~in_3);  // OR_Gate
  and and_2 (and_2_out, d_latch_1_out_3, in_3);
  D_latch d_latch_2 (.CLK(or_2_out), .D(and_2_out), .out_3(out_4), .out_4(out_5));
endmodule

module _9_0_subtractor (
  input  in_1,
  input  in_2,
  output [3:0] out_3
);

  wire nor_1_out;
  wire [2:1] or_1_out;
  wire [3:0] n4_bit_register_1_out_4;

  or or_1 (or_1_out[1], 1'b0, nor_1_out);
  or or_2 (or_1_out[2], 1'b0, nor_1_out);
  Subtractor #(.width(4)) subtractor_1 (
    .a(n4_bit_register_1_out_4), .b({1'b0, or_1_out, 1'b1}), .out(out_3));  // open: bin, bout
  _4_bit_register u_4_bit_register_1 (.in_1(out_3), .out_4(n4_bit_register_1_out_4), .in_2(in_1), .in_3(in_2));
  nor nor_1 (nor_1_out, n4_bit_register_1_out_4[3], n4_bit_register_1_out_4[2], n4_bit_register_1_out_4[1], n4_bit_register_1_out_4[0]);
endmodule

module dff_sync_set (
  input  clock,
  input  in_2,
  input  set,
  output out_4,
  output out_5
);

  wire or_1_out;

  or or_1 (or_1_out, in_2, ~set);  // OR_Gate
  D_flip_flop d_flip_flop_1 (.in_1(clock), .in_2(or_1_out), .out_3(out_4), .out_4(out_5));
endmodule
