// Logisim project counter.circ as structural Verilog: 2 circuits, main circuit main
module main (
  input  CLK,
  input  SW,
  input  RST
);

  wire not_1_out, or_1_out, pulse_1_pulse, pulse_2_pulse;
  wire [3:0] adder_1_out, register_1_q;

  pulse pulse_1 (.CLK(CLK), .sw(SW), .pulse(pulse_1_pulse));
  pulse pulse_2 (.CLK(CLK), .sw(not_1_out), .pulse(pulse_2_pulse));
  not not_1 (not_1_out, SW);
  or or_1 (or_1_out, pulse_1_pulse, pulse_2_pulse);
  // Probe on adder_1_out
  Adder #(.width(4)) adder_1 (.a(4'b0000), .b(register_1_q), .out(adder_1_out), .cin(or_1_out));  // open: cout
  Register #(.width(4)) register_1 (.D(adder_1_out), .Q(register_1_q), .clk(CLK), .clr(RST));  // open: en
endmodule

module pulse (
  input  CLK,
  input  sw,
  output pulse
);

  wire d_ff_1_q, d_ff_2_q;

  D_Flip_Flop d_ff_1 (.clk(CLK), .D(sw), .Q(d_ff_1_q));  // open: Qn, preset, en, reset
  D_Flip_Flop d_ff_2 (.clk(CLK), .D(d_ff_1_q), .Q(d_ff_2_q));  // open: Qn, preset, en, reset
  and and_1 (pulse, ~d_ff_2_q, d_ff_1_q);  // AND_Gate
endmodule
